// Logisim project sbc6526.circ as structural Verilog: 2 circuits, main circuit sbc6526
module sbc6526 (
  input  RDY,
  input  BE,
  input  [7:0] in_3,
  input  [7:0] in_4,
  input  in_5,
  input  in_6,
  output [15:0] out_7,
  output [7:0] out_8,
  output [7:0] out_9,
  output out_10
);

  wire button_1_out, button_2_out, button_3_out, clock_1_out, memdecoder_1_ncia, memdecoder_1_nciares,
       memdecoder_1_oe, memdecoder_1_we, n6502_1_phi2, n6502_1_r_w, not_1_out, not_2_out, not_3_out, TERM;
  wire [7:0] n6502_1_d_out;

  Clock clock_1 (.out(clock_1_out));
  _6502 u_6502_1 (
    .A_BUS(out_7), .D_OUT(n6502_1_d_out), .R_W(n6502_1_r_w), .PHI2(n6502_1_phi2), .PHI0(clock_1_out),
    .RDY(RDY), .BE(BE), .nRS(not_1_out), .nIRQ(not_2_out), .nNMI(not_3_out), .D_IN(n6502_1_d_out));  // open: AX_OUT, PHI1, SYNC
  not not_1 (not_1_out, button_3_out);
  not not_2 (not_2_out, button_1_out);
  Button button_1 (.out(button_1_out));
  not not_3 (not_3_out, button_2_out);
  Button button_2 (.out(button_2_out));
  Button button_3 (.out(button_3_out));
  TTY #(.asciiwidth(8), .cols(20)) tty_1 (.data(n6502_1_d_out[6:0]), .clk(TERM), .clr(button_3_out));  // open: we
  memDecoder memdecoder_1 (
    .A(out_7), .R_W(n6502_1_r_w), .PHI2(n6502_1_phi2), .OE(memdecoder_1_oe), .WE(memdecoder_1_we),
    .nCIA(memdecoder_1_ncia), .TERM(TERM), .nCIARES(memdecoder_1_nciares));
  // RAM #(.addrWidth(16), .databus("bidir"), .trigger("high"), .\type ("nonvolatile")) ram_1: pin names not known; wires that end beside it: out_7, memdecoder_1_oe, memdecoder_1_we, 1'b1, n6502_1_d_out
  _74hct6526 _6526 (
    .oD(n6502_1_d_out), .PAO(out_8), .PBO(out_9), .nPC(out_10), .iD(n6502_1_d_out), .A(out_7), .nFLAG(in_5),
    .PAI(in_3), .PBI(in_4), .nCS(memdecoder_1_ncia), .PHI2(n6502_1_phi2), .TOD(in_6), .RnW(n6502_1_r_w),
    .nRES(memdecoder_1_nciares));  // open: oCNT, oSP, nIRQ, iSP, CNT
  // Pins of 7 and 8 bits meet at n6502_1_d_out

  // Notes on the sheet:
  //   PHI0
  //   IRQ
  //   NMI
  //   addr
  //   PHI1
  //   PHI2
  //   R/W
  //   SYNC
  //   DATA
endmodule

module memDecoder (
  input  [15:0] A,
  input  R_W,
  input  PHI2,
  output OE,
  output WE,
  output nCIA,
  output TERM,
  output nCIARES
);

  wire and_1_out, decoder_1_out2, decoder_2_out1, not_2_out;
  wire [0:0] not_1_out;

  and and_1 (and_1_out, A[15], ~A[14]);  // AND_Gate
  not not_1 (not_1_out[0], PHI2);
  Decoder #(.enable("false"), .select(2)) decoder_1 (.out2(decoder_1_out2), .sel(A[15:14]));  // open: out0, out1, out3
  Decoder #(.select(3)) decoder_2 (
    .out1(decoder_2_out1), .sel(A[13:11]), .en(and_1_out));  // open: out0, out2, out3, out4, out5, out6, out7
  Decoder #(.select(2)) decoder_3 (
    .out0(WE), .out2(OE), .sel({R_W, not_1_out[0]}), .en(not_2_out));  // open: out1, out3
  nand nand_1 (nCIARES, WE, ~A[15], A[14], ~A[13], ~A[12]);  // NAND_Gate
  and u_TERM (TERM, WE, ~A[15], A[14], A[13], A[12]);  // AND_Gate
  not not_2 (not_2_out, decoder_1_out2);
  not not_3 (nCIA, decoder_2_out1);
endmodule
